# Fritzing sketch skema (saved by Fritzing 0.9.3b)

parts:
  A1 = TS-300B interface
  HC-SR04_Sensor_1 = HC-SR04 Ultrasonic Distance Sensor
  J1 = Basic Servo
  J2 = Basic Servo
  Part1 = Arduino BT
  LCD2004-I2C1 = LCD2004-I2C
  S1 = PH meter [package=THT]
  S2 = Round Pushbutton
  S3 = Round Pushbutton
  S4 = Round Pushbutton
  S5 = Round Pushbutton
  DS1 = DS18B20 1-Wire Temperature Sensor [part_number=DS18B20]
  R1 = Resistor [tolerance=±5% resistance=220 package="2010 [SMD]"]
  RY1 = SSR-40VA
  RTC1 = DS3231 AT24C32 Real Time Clock  # not connected
  M1 = 1 chan 5v relay module
  LED1 = LEDs [package=led10mm]
  LED2 = LEDs [package=led10mm]
  J3 = Piezo Speaker

nets:
  N1: A1.Pin_2, Part1.A0
  VCC: HC-SR04_Sensor_1.VCC, Part1.5V, LCD2004-I2C1.VCC
  N2: HC-SR04_Sensor_1.TRIG, Part1.PWM_D3
  N3: HC-SR04_Sensor_1.ECHO, Part1.D4
  N4: J1.pulse, Part1.PWM_D9
  N5: J2.pulse, Part1.RESET_WT11/D7
  N6: Part1.D8, R1.Pin_1
  N7: Part1.SS/PWM_D10, S3.leg1
  N8: Part1.MOSI/PWM_D11, S4.leg1
  N9: Part1.MISO/D12, S5.leg1
  N10: Part1.SCK/D13, J3.pin2
  N11: Part1.A1, S1.pin1
  N12: Part1.A2, RY1.Pin_3
  N13: Part1.A4, LCD2004-I2C1.SDA
  N14: Part1.A5, LCD2004-I2C1.SCL
  N15: Part1.TX/D1, LED2.C
  N16: Part1.D2, S2.leg1
  N17: Part1.PWM_D5, M1.pin_3
  N18: Part1.PWM_D6, LED1.C
  GND: Part1.GND, LCD2004-I2C1.GND, S2.leg0
  N19: DS1.VDD, M1.pin_1

custom parts:
  TS-300B interface: TS-300B interface.
  LCD2004-I2C: A standard character display with 4x20 characters. Comes in many colors with LCM2004 IIC attached.
  SSR-40VA: SSR-40VA solid state relay.
  DS3231 AT24C32 Real Time Clock: Real-time clock basedo on chip DS3231, plus memory chip AT24C32 (32 Kb storage capacity). On-chip temperature sensor with an accuracy of ±3 ℃, I2C bus interface maximum speed: 400 kHz. Operating voltage: 3.3 V to 5.5 V with battery backup capabilities.
  1 chan 5v relay module: 1 Channel 5V Relay Module Board Shield with Optocoupler Support High and Low Level Trigger for Arduino.
